# Fritzing sketch Schematic (saved by Fritzing 0.9.9b)
breadboards: 1

parts:
  Argon1 = Particle Argon
  Part1 = Analog Digital MUX Breakout
  R1 = Basic Flex Resistor
  R2 = Basic Flex Resistor
  R3 = Basic Flex Resistor
  R4 = Basic Flex Resistor
  R5 = Basic Flex Resistor
  R6 = Basic Flex Resistor
  R7 = Basic Flex Resistor
  R8 = Basic Flex Resistor
  R9 = Basic Flex Resistor
  R10 = Basic Flex Resistor
  R21 = Trimmer Potentiometer [maximum_resistance=10kΩ package=THT]
  R22 = Trimmer Potentiometer [maximum_resistance=10kΩ package=THT]
  R23 = Trimmer Potentiometer [maximum_resistance=10kΩ package=THT]
  R24 = Trimmer Potentiometer [maximum_resistance=10kΩ package=THT]
  R25 = Trimmer Potentiometer [maximum_resistance=10kΩ package=THT]
  R26 = Trimmer Potentiometer [maximum_resistance=10kΩ package=THT]
  R27 = Trimmer Potentiometer [maximum_resistance=10kΩ package=THT]
  R28 = Trimmer Potentiometer [maximum_resistance=10kΩ package=THT]
  R29 = Trimmer Potentiometer [maximum_resistance=10kΩ package=THT]
  R30 = Trimmer Potentiometer [maximum_resistance=10kΩ package=THT]

nets:
  3.3V: Argon1.3.3V, Part1.VCC, R21.leg2, R22.leg2, R23.leg2, R24.leg2, R25.leg2, R26.leg2, R27.leg2, R28.leg2, R29.leg2, R30.leg2
  GND: Argon1.GND, Part1.GND, Part1.EN, R1.pin_1, R2.pin_1, R3.pin_1, R4.pin_1, R5.pin_1, R6.pin_1, R7.pin_1, R8.pin_1, R9.pin_1, R10.pin_1
  N1: Argon1.A5, Part1.SIG
  N2: Argon1.D2, Part1.S0
  N3: Argon1.D3, Part1.S1
  N4: Argon1.D4, Part1.S2
  N5: Argon1.D5, Part1.S3
  N6: Part1.C6, R1.Pin_2, R30.wiper
  N7: Part1.C7, R2.Pin_2, R29.wiper
  N8: Part1.C8, R3.Pin_2, R28.wiper
  N9: Part1.C9, R4.Pin_2, R27.wiper
  N10: Part1.C10, R5.Pin_2, R26.wiper
  N11: Part1.C11, R6.Pin_2, R25.wiper
  N12: Part1.C12, R8.Pin_2, R21.wiper
  N13: Part1.C13, R7.Pin_2, R22.wiper
  N14: Part1.C14, R9.Pin_2, R23.wiper
  N15: Part1.C15, R10.Pin_2, R24.wiper

notes:
  Pointer
  Middle
  Ring
  Pinky
  Hand Arch
  Thumb

custom parts:
  Particle Argon: The Argon is a powerful Wi-Fi enabled development board that can act as either a standalone Wi-Fi endpoint or Wi-Fi enabled gateway for Particle Mesh networks. It is based on the Nordic nRF52840 and has built-in battery charging circuitry so it’s easy to connect a Li-Po and deploy your local network in minutes. The Argon is great for connecting existing projects to the Particle Device Cloud or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
